// Logisim project alu.circ as structural Verilog: 14 circuits, main circuit alu
module alu (
  input  [31:0] A,
  input  [31:0] B,
  input  [3:0] ALUSel,
  output [31:0] ALUResult
);

  wire [31:0] add0_out, and0_out, bsel0_out, mul0_out, mulh_out, mulhu_out, or0_out, sll0_out, slt0_out,
       sra0_out, srl0_out, sub0_out, xor0_out;

  Multiplexer #(.select(4), .width(32)) multiplexer_1 (
    .in0(add0_out), .in1(sll0_out), .in2(slt0_out), .in4(xor0_out), .in5(srl0_out), .in6(or0_out),
    .in7(and0_out), .in8(mul0_out), .in9(mulh_out), .in11(mulhu_out), .in12(sub0_out), .in13(sra0_out),
    .in15(bsel0_out), .out(ALUResult), .sel(ALUSel));  // open: in3, in10, in14
  add0 add0_1 (.A(A), .B(B), .out_3(add0_out));
  sll0 sll0_1 (.A(A), .B(B), .out_3(sll0_out));
  slt0 slt0_1 (.A(A), .B(B), .out_3(slt0_out));
  xor0 xor0_1 (.A(A), .B(B), .out_3(xor0_out));
  srl0 srl0_1 (.A(A), .B(B), .out_3(srl0_out));
  or0 or0_1 (.A(A), .B(B), .out_3(or0_out));
  and0 and0_1 (.A(A), .B(B), .out_3(and0_out));
  mul0 mul0_1 (.A(A), .B(B), .out_3(mul0_out));
  bsel0 bsel0_1 (.B(B), .out_2(bsel0_out));
  mulh mulh_1 (.A(A), .B(B), .out_3(mulh_out));
  mulhu mulhu_1 (.A(A), .B(B), .out_3(mulhu_out));
  sub0 sub0_1 (.A(A), .B(B), .out_3(sub0_out));
  sra0 sra0_1 (.A(A), .B(B), .out_3(sra0_out));

  // Notes on the sheet:
  //   INPUTS to your circuit
  //   DON'T CHANGE THE LOCATIONS OF THE INPUTS AND OUTPUTS!
  //   OUTPUT from your circuit
endmodule

module add0 (
  input  [31:0] A,
  input  [31:0] B,
  output [31:0] out_3
);

  Adder #(.width(32)) adder_1 (.a(A), .b(B), .out(out_3));  // open: cin, cout
endmodule

module sll0 (
  input  [31:0] A,
  input  [31:0] B,
  output [31:0] out_3
);

  wire [4:0] bit_extender_1_out;

  Bit_Extender #(.in_width(32), .out_width(5)) bit_extender_1 (.in(B), .out(bit_extender_1_out));
  Shifter #(.width(32)) shifter_1 (.in(A), .\dist (bit_extender_1_out), .out(out_3));
endmodule

module slt0 (
  input  [31:0] A,
  input  [31:0] B,
  output [31:0] out_3
);

  wire comparator_1_lt;

  Comparator #(.width(32)) comparator_1 (.a(A), .b(B), .lt(comparator_1_lt));  // open: gt, eq
  assign out_3 = {{31{1'b0}}, comparator_1_lt};  // Bit_Extender bit_extender_1
endmodule

module xor0 (
  input  [31:0] A,
  input  [31:0] B,
  output [31:0] out_3
);

  assign out_3 = A ^ B;  // XOR_Gate xor_1, 32 bits wide
endmodule

module srl0 (
  input  [31:0] A,
  input  [31:0] B,
  output [31:0] out_3
);

  wire [4:0] bit_extender_1_out;

  Bit_Extender #(.in_width(32), .out_width(5)) bit_extender_1 (.in(B), .out(bit_extender_1_out));
  Shifter #(.shift("lr"), .width(32)) shifter_1 (.in(A), .\dist (bit_extender_1_out), .out(out_3));
endmodule

module or0 (
  input  [31:0] A,
  input  [31:0] B,
  output [31:0] out_3
);

  assign out_3 = A | B;  // OR_Gate or_1, 32 bits wide
endmodule

module and0 (
  input  [31:0] A,
  input  [31:0] B,
  output [31:0] out_3
);

  assign out_3 = A & B;  // AND_Gate and_1, 32 bits wide
endmodule

module mul0 (
  input  [31:0] A,
  input  [31:0] B,
  output [31:0] out_3
);

  Multiplier #(.mode("twosComplement"), .width(32)) multiplier_1 (.a(A), .b(B), .out(out_3));  // open: cin, cout
endmodule

module mulh (
  input  [31:0] A,
  input  [31:0] B,
  output [31:0] out_3
);

  Multiplier #(.mode("twosComplement"), .width(32)) multiplier_1 (.a(A), .b(B), .cout(out_3));  // open: out, cin
endmodule

module mulhu (
  input  [31:0] A,
  input  [31:0] B,
  output [31:0] out_3
);

  Multiplier #(.width(32)) multiplier_1 (.a(A), .b(B), .cout(out_3));  // open: out, cin
endmodule

module sub0 (
  input  [31:0] A,
  input  [31:0] B,
  output [31:0] out_3
);

  Subtractor #(.width(32)) subtractor_1 (.a(A), .b(B), .out(out_3));  // open: bin, bout
endmodule

module sra0 (
  input  [31:0] A,
  input  [31:0] B,
  output [31:0] out_3
);

  wire [4:0] bit_extender_1_out;

  Bit_Extender #(.in_width(32), .out_width(5)) bit_extender_1 (.in(B), .out(bit_extender_1_out));
  Shifter #(.shift("ar"), .width(32)) shifter_1 (.in(A), .\dist (bit_extender_1_out), .out(out_3));
endmodule

module bsel0 (
  input  [31:0] B,
  output [31:0] out_2
);


  assign out_2 = B;
endmodule
