// Logisim project control-logic.circ as structural Verilog: 7 circuits, main circuit control_logic
module control_logic (
  input  [31:0] Instruction,
  input  BrEq,
  input  BrLt,
  output PCSel,
  output RegWEn,
  output [2:0] ImmSel,
  output BrUn,
  output ASel,
  output BSel,
  output [3:0] ALUSel,
  output MemWEn,
  output [1:0] WBSel
);

  wire ASel_implied;
  wire [2:0] funct3;
  wire [4:0] rd, rs1, rs2;
  wire [6:0] funct7, opcode;
  wire [15:0] rom_1_data;

  ROM #(.addrWidth(6), .dataWidth(16)) rom_1 (.data(rom_1_data));  // open: addr
  ID id_1 (
    .Instruction(Instruction), .opcode(opcode), .rd(rd), .funct3(funct3), .rs1(rs1), .rs2(rs2),
    .funct7(funct7), .RegWEn(RegWEn), .BSel(BSel), .ASel_implied(ASel_implied), .ImmSel(ImmSel),
    .MemWEn(MemWEn));
  functs_to_ALUSel functs_to_alusel_1 (.funct7(funct7), .funct3(funct3), .opcode(opcode), .ALUSel(ALUSel));
  opcode_funct3_to_BrUn opcode_funct3_to_brun_1 (.opcode(opcode), .funct3(funct3), .BrUn(BrUn));
  ASel_to_PCSel asel_to_pcsel_1 (.Instruction(Instruction), .ASel(ASel), .PCSel(PCSel));
  ASel_checker asel_checker_1 (
    .beq(BrEq), .blt(BrLt), .ASel_implied(ASel_implied), .opcode(opcode), .funct3(funct3), .ASel(ASel));
  WBSel_checker wbsel_checker_1 (.opcode(opcode), .funct3(funct3), .WBSel(WBSel));

  // Notes on the sheet:
  //   INPUTS to your circuit
  //   Connect ROM Input here ->
  //   ROM FOR CONTROL LOGIC
  //   DON'T CHANGE THE LOCATIONS OF THE INPUTS AND OUTPUTS!
  //   This is only if you choose to do the ROM option
  //   CONNECT
  //   WIRE
  //   TO
  //   USE
  //   ROM
  //   OUTPUT from your circuit
  //   Reminder: If using ROM, use combinational logic for PCSel
endmodule

module ID (
  input  [31:0] Instruction,
  output [6:0] opcode,
  output [4:0] rd,
  output [2:0] funct3,
  output [4:0] rs1,
  output [4:0] rs2,
  output [6:0] funct7,
  output RegWEn,
  output BSel,
  output ASel_implied,
  output [2:0] ImmSel,
  output MemWEn
);

  wire ASel_B, ASel_J, BSel_I, BSel_I_star, BSel_J, BSel_U, comparator_1_eq, comparator_2_eq,
       comparator_3_eq, comparator_4_eq, comparator_5_eq, comparator_6_eq, comparator_7_eq, RegWEn_R;
  wire [2:0] demultiplexer_5_out1, funct3_B, funct3_I, funct3_I_star, funct3_R, funct3_S, ImmSel_B, ImmSel_I,
       ImmSel_J, ImmSel_S, ImmSel_U;
  wire [4:0] imm5_B, imm5_I_star, imm5_S, rd_I, rd_I_star, rd_J, rd_R, rd_U, rs1_B, rs1_I, rs1_I_star, rs1_R,
       rs1_S, rs2_B, rs2_R, rs2_S;
  wire [6:0] funct7_I_star, funct7_R, imm7_B, imm7_S, opcode_B, opcode_I, opcode_I_star, opcode_J, opcode_R,
       opcode_S, opcode_U;
  wire [11:0] imm12_I;
  wire [19:0] imm20_J, imm20_U;

  Comparator #(.width(7)) comparator_1 (.a(Instruction[6:0]), .b(7'b0010011), .eq(comparator_1_eq));  // open: gt, lt
  Comparator #(.width(7)) comparator_2 (.a(Instruction[6:0]), .b(7'b0000011), .eq(comparator_2_eq));  // open: gt, lt
  Comparator #(.width(7)) comparator_3 (.a(Instruction[6:0]), .b(7'b1100111), .eq(comparator_3_eq));  // open: gt, lt
  Comparator #(.width(7)) comparator_4 (.a(Instruction[6:0]), .b(7'b0010111), .eq(comparator_4_eq));  // open: gt, lt
  Comparator #(.width(7)) comparator_5 (.a(Instruction[6:0]), .b(7'b0110111), .eq(comparator_5_eq));  // open: gt, lt
  Comparator #(.width(7)) comparator_6 (.a(Instruction[6:0]), .b(7'b1101111), .eq(comparator_6_eq));  // open: gt, lt
  Comparator #(.width(7)) comparator_7 (.a(Instruction[6:0]), .b(7'b1100111), .eq(comparator_7_eq));  // open: gt, lt
  or or_1 (BSel_I, comparator_1_eq, comparator_2_eq, comparator_3_eq);
  Demultiplexer #(.width(3)) demultiplexer_1 (.out1(ImmSel_I), .in(3'b000), .sel(BSel_I));  // open: out0
  Comparator #(.width(7)) comparator_8 (.a(Instruction[6:0]), .b(7'b0110011), .eq(RegWEn_R));  // open: gt, lt
  Comparator #(.width(7)) comparator_9 (.a(Instruction[6:0]), .b(7'b0010011), .eq(BSel_I_star));  // open: gt, lt
  Comparator #(.width(7)) comparator_10 (.a(Instruction[6:0]), .b(7'b0100011), .eq(MemWEn));  // open: gt, lt
  Demultiplexer #(.width(3)) demultiplexer_2 (.out1(ImmSel_S), .in(3'b001), .sel(MemWEn));  // open: out0
  Comparator #(.width(7)) comparator_11 (.a(Instruction[6:0]), .b(7'b1100011), .eq(ASel_B));  // open: gt, lt
  Demultiplexer #(.width(3)) demultiplexer_3 (.out1(ImmSel_B), .in(3'b010), .sel(ASel_B));  // open: out0
  or or_2 (BSel_U, comparator_4_eq, comparator_5_eq);
  Demultiplexer #(.width(3)) demultiplexer_4 (.out1(ImmSel_U), .in(3'b011), .sel(BSel_U));  // open: out0
  or or_3 (BSel_J, comparator_6_eq, comparator_7_eq);
  Demultiplexer #(.width(3)) demultiplexer_5 (.out1(demultiplexer_5_out1), .in(3'b100), .sel(BSel_J));  // open: out0
  Multiplexer #(.width(3)) multiplexer_1 (
    .in0(demultiplexer_5_out1), .in1(3'b000), .out(ImmSel_J), .sel(comparator_7_eq));
  Demultiplexer #(.enable("true"), .width(32)) demultiplexer_6 (
    .out1({imm12_I, rs1_I, funct3_I, rd_I, opcode_I}), .in(Instruction), .sel(BSel_I), .en(BSel_I));  // open: out0
  Demultiplexer #(.enable("true"), .width(32)) demultiplexer_7 (
    .out1({funct7_R, rs2_R, rs1_R, funct3_R, rd_R, opcode_R}), .in(Instruction), .sel(RegWEn_R), .en(RegWEn_R));  // open: out0
  Demultiplexer #(.enable("true"), .width(32)) demultiplexer_8 (
    .out1({funct7_I_star, imm5_I_star, rs1_I_star, funct3_I_star, rd_I_star, opcode_I_star}),
    .in(Instruction), .sel(BSel_I_star), .en(BSel_I_star));  // open: out0
  Demultiplexer #(.enable("true"), .width(32)) demultiplexer_9 (
    .out1({imm7_S, rs2_S, rs1_S, funct3_S, imm5_S, opcode_S}), .in(Instruction), .sel(MemWEn), .en(MemWEn));  // open: out0
  Demultiplexer #(.enable("true"), .width(32)) demultiplexer_10 (
    .out1({imm7_B, rs2_B, rs1_B, funct3_B, imm5_B, opcode_B}), .in(Instruction), .sel(ASel_B), .en(ASel_B));  // open: out0
  Demultiplexer #(.enable("true"), .width(32)) demultiplexer_11 (
    .out1({imm20_U, rd_U, opcode_U}), .in(Instruction), .sel(BSel_U), .en(BSel_U));  // open: out0
  Demultiplexer #(.enable("true"), .width(32)) demultiplexer_12 (
    .out1({imm20_J, rd_J, opcode_J}), .in(Instruction), .sel(BSel_J), .en(BSel_J));  // open: out0
  Multiplexer multiplexer_2 (.in0(BSel_J), .in1(1'b0), .out(ASel_J), .sel(comparator_7_eq));
  assign opcode = opcode_I | opcode_R | opcode_I_star | opcode_S | opcode_B | opcode_U | opcode_J;  // OR_Gate or_4, 7 bits wide
  assign rd = rd_I | rd_R | rd_I_star | rd_U | rd_J;  // OR_Gate or_5, 5 bits wide
  assign funct3 = funct3_R | funct3_I | funct3_I_star | funct3_S | funct3_B;  // OR_Gate or_6, 3 bits wide
  assign rs1 = rs1_R | rs1_I | rs1_I_star | rs1_S | rs1_B;  // OR_Gate or_7, 5 bits wide
  assign rs2 = rs2_R | rs2_S | rs2_B;  // OR_Gate or_8, 5 bits wide
  assign funct7 = funct7_R | funct7_I_star;  // OR_Gate or_9, 7 bits wide
  or or_10 (RegWEn, RegWEn_R, BSel_I, BSel_I_star, BSel_U, BSel_J);
  or or_11 (BSel, BSel_I, BSel_I_star, BSel_U, BSel_J, ASel_B, MemWEn);
  or or_12 (ASel_implied, ASel_B, ASel_J);
  assign ImmSel = ImmSel_J | ImmSel_I | ImmSel_S | ImmSel_B | ImmSel_U;  // OR_Gate or_13, 3 bits wide

  // Other names for the same wires on the sheet: BSel_B = ASel_B; BSel_S = MemWEn; Opcode_t[6:0] = Instruction[6:0];
  //   RegWEn_I = BSel_I; RegWEn_I_star = BSel_I_star; RegWEn_J = BSel_J; RegWEn_U = BSel_U
endmodule

module functs_to_ALUSel (
  input  [6:0] funct7,
  input  [2:0] funct3,
  input  [6:0] opcode,
  output [3:0] ALUSel
);

  wire and_1_out, comparator_1_eq, comparator_2_eq, comparator_3_eq, comparator_4_eq, comparator_5_eq,
       comparator_6_eq, comparator_7_eq, comparator_8_eq, comparator_9_eq, comparator_10_eq,
       comparator_11_eq, comparator_12_eq, comparator_13_eq, comparator_14_eq, comparator_15_eq, not_1_out,
       or_1_out, or_2_out;
  wire [3:0] ALUSel0_out, ALUSel1_out, ALUSel2_out, ALUSel3_out, ALUSel4_out, ALUSel5_out, ALUSel6_out,
       ALUSel7_out, multiplexer_1_out, multiplexer_4_out, multiplexer_5_out, multiplexer_6_out,
       multiplexer_8_out, multiplexer_9_out, multiplexer_10_out;

  Comparator #(.width(7)) comparator_1 (.a(funct7), .b({7{1'b0}}), .eq(comparator_1_eq));  // open: gt, lt
  Comparator #(.width(7)) comparator_2 (.a(funct7), .b({7{1'b0}}), .eq(comparator_2_eq));  // open: gt, lt
  Comparator #(.width(7)) comparator_3 (.a(funct7), .b({7{1'b0}}), .eq(comparator_3_eq));  // open: gt, lt
  assign ALUSel2_out = {{1{1'b0}}, funct3};  // Bit_Extender bit_extender_1
  assign ALUSel3_out = {{1{1'b0}}, funct3};  // Bit_Extender bit_extender_2
  assign ALUSel4_out = {{1{1'b0}}, funct3};  // Bit_Extender bit_extender_3
  assign ALUSel6_out = {{1{1'b0}}, funct3};  // Bit_Extender bit_extender_4
  assign ALUSel7_out = {{1{1'b0}}, funct3};  // Bit_Extender bit_extender_5
  Multiplexer #(.width(4)) multiplexer_1 (.in0(4'b1100), .in1(4'b0000), .out(multiplexer_1_out), .sel(comparator_1_eq));
  Comparator #(.width(7)) comparator_4 (.a(funct7), .b(7'b0000001), .eq(comparator_4_eq));  // open: gt, lt
  Multiplexer #(.width(4)) multiplexer_2 (.in0(4'b1001), .in1(4'b0001), .out(ALUSel1_out), .sel(comparator_2_eq));
  Multiplexer #(.width(4)) multiplexer_3 (.in0(4'b1101), .in1(4'b0101), .out(ALUSel5_out), .sel(comparator_3_eq));
  Multiplexer #(.width(4)) multiplexer_4 (
    .in0(multiplexer_1_out), .in1(4'b1000), .out(multiplexer_4_out), .sel(comparator_4_eq));
  Comparator #(.width(7)) comparator_5 (.a(funct7), .b(7'b0100000), .eq(comparator_5_eq));  // open: gt, lt
  Multiplexer #(.select(3), .width(4)) multiplexer_5 (
    .in0(ALUSel0_out), .in1(ALUSel1_out), .in2(ALUSel2_out), .in3(ALUSel3_out), .in4(ALUSel4_out),
    .in5(ALUSel5_out), .in6(ALUSel6_out), .in7(ALUSel7_out), .out(multiplexer_5_out), .sel(funct3));
  Multiplexer #(.width(4)) multiplexer_6 (
    .in0(multiplexer_4_out), .in1(4'b1100), .out(multiplexer_6_out), .sel(comparator_5_eq));
  Multiplexer #(.width(4)) multiplexer_7 (
    .in0(multiplexer_6_out), .in1(ALUSel2_out), .out(ALUSel0_out), .sel(not_1_out));
  not not_1 (not_1_out, comparator_6_eq);
  Comparator #(.width(7)) comparator_6 (.a(opcode), .b(7'b0110011), .eq(comparator_6_eq));  // open: gt, lt
  Comparator #(.width(7)) comparator_7 (.a(7'b1100011), .b(opcode), .eq(comparator_7_eq));  // open: gt, lt
  Comparator #(.width(7)) comparator_8 (.a(opcode), .b(7'b1101111), .eq(comparator_8_eq));  // open: gt, lt
  Comparator #(.width(7)) comparator_9 (.a(opcode), .b(7'b0000011), .eq(comparator_9_eq));  // open: gt, lt
  or or_1 (or_1_out, comparator_7_eq, comparator_8_eq, comparator_9_eq);
  Comparator #(.width(7)) comparator_10 (.a(7'b0100011), .b(opcode), .eq(comparator_10_eq));  // open: gt, lt
  Comparator #(.width(7)) comparator_11 (.a(7'b1100111), .b(opcode), .eq(comparator_11_eq));  // open: gt, lt
  Multiplexer #(.width(4)) multiplexer_8 (
    .in0(multiplexer_5_out), .in1(4'b0000), .out(multiplexer_8_out), .sel(or_1_out));
  or or_2 (or_2_out, comparator_10_eq, comparator_11_eq);
  Multiplexer #(.width(4)) multiplexer_9 (
    .in0(multiplexer_8_out), .in1(4'b0000), .out(multiplexer_9_out), .sel(or_2_out));
  Comparator #(.width(7)) comparator_12 (.a(7'b1101111), .b(opcode), .eq(comparator_12_eq));  // open: gt, lt
  Multiplexer #(.width(4)) multiplexer_10 (
    .in0(multiplexer_9_out), .in1(4'b0000), .out(multiplexer_10_out), .sel(comparator_12_eq));
  Multiplexer #(.width(4)) multiplexer_11 (.in0(multiplexer_10_out), .in1(4'b1011), .out(ALUSel), .sel(and_1_out));
  Comparator #(.width(7)) comparator_13 (.a(7'b0110011), .b(opcode), .eq(comparator_13_eq));  // open: gt, lt
  Comparator #(.width(3)) comparator_14 (.a(3'b011), .b(funct3), .eq(comparator_14_eq));  // open: gt, lt
  Comparator #(.width(7)) comparator_15 (.a(7'b0000001), .b(funct7), .eq(comparator_15_eq));  // open: gt, lt
  and and_1 (and_1_out, comparator_13_eq, comparator_14_eq, comparator_15_eq);
endmodule

module opcode_funct3_to_BrUn (
  input  [6:0] opcode,
  input  [2:0] funct3,
  output BrUn
);

  wire comparator_1_eq, comparator_2_eq, or_1_out;

  Comparator #(.width(10)) comparator_1 (.a(10'h263), .b({funct3, opcode}), .eq(comparator_1_eq));  // open: gt, lt
  Comparator #(.width(10)) comparator_2 (.a({funct3, opcode}), .b(10'h2e3), .eq(comparator_2_eq));  // open: gt, lt
  or or_1 (or_1_out, comparator_1_eq, comparator_2_eq);
  not not_1 (BrUn, or_1_out);
endmodule

module ASel_checker (
  input  beq,
  input  blt,
  input  ASel_implied,
  input  [6:0] opcode,
  input  [2:0] funct3,
  output ASel
);

  wire and_1_out, and_2_out, and_3_out, and_4_out, and_5_out, and_6_out, and_7_out, and_8_out,
       comparator_1_eq, comparator_2_eq, comparator_3_eq, comparator_4_eq, comparator_5_eq, comparator_6_eq,
       comparator_7_eq, comparator_8_eq, comparator_9_eq, comparator_10_eq, comparator_11_eq, funct3_implied,
       not_1_out, not_2_out, not_3_out, not_4_out, or_2_out;

  Comparator #(.width(3)) comparator_1 (.a(3'b000), .b(funct3), .eq(comparator_1_eq));  // open: gt, lt
  Comparator #(.width(1)) comparator_2 (.a(1'b1), .b(beq), .eq(comparator_2_eq));  // open: gt, lt
  Comparator #(.width(3)) comparator_3 (.a(3'b100), .b(funct3), .eq(comparator_3_eq));  // open: gt, lt
  Comparator #(.width(1)) comparator_4 (.a(1'b1), .b(blt), .eq(comparator_4_eq));  // open: gt, lt
  Comparator #(.width(3)) comparator_5 (.a(3'b110), .b(funct3), .eq(comparator_5_eq));  // open: gt, lt
  Comparator #(.width(1)) comparator_6 (.a(1'b1), .b(blt), .eq(comparator_6_eq));  // open: gt, lt
  Comparator #(.width(3)) comparator_7 (.a(3'b101), .b(funct3), .eq(comparator_7_eq));  // open: gt, lt
  not not_1 (not_1_out, blt);
  Comparator #(.width(3)) comparator_8 (.a(3'b111), .b(funct3), .eq(comparator_8_eq));  // open: gt, lt
  not not_2 (not_2_out, blt);
  Comparator #(.width(3)) comparator_9 (.a(3'b001), .b(funct3), .eq(comparator_9_eq));  // open: gt, lt
  not not_3 (not_3_out, beq);
  and and_1 (and_1_out, comparator_1_eq, comparator_2_eq);
  and and_2 (and_2_out, comparator_3_eq, comparator_4_eq);
  and and_3 (and_3_out, comparator_5_eq, comparator_6_eq);
  and and_4 (and_4_out, comparator_8_eq, not_2_out);
  and and_5 (and_5_out, comparator_9_eq, not_3_out);
  and and_6 (and_6_out, comparator_7_eq, not_1_out);
  or or_1 (funct3_implied, and_1_out, and_2_out, and_3_out, and_6_out, and_4_out, and_5_out);
  Comparator #(.width(7)) comparator_10 (.a(opcode), .b(7'b1100011), .eq(comparator_10_eq));  // open: gt, lt
  and and_7 (and_7_out, funct3_implied, comparator_10_eq);
  not not_4 (not_4_out, comparator_10_eq);
  or or_2 (or_2_out, and_7_out, not_4_out);
  and and_8 (and_8_out, or_2_out, ASel_implied);
  Comparator #(.width(7)) comparator_11 (.a(opcode), .b(7'b0010111), .eq(comparator_11_eq));  // open: gt, lt
  or or_3 (ASel, and_8_out, comparator_11_eq);
endmodule

module WBSel_checker (
  input  [6:0] opcode,
  input  [2:0] funct3,
  output [1:0] WBSel
);

  wire comparator_1_eq, comparator_2_eq;
  wire [1:0] or_1_out;

  Comparator #(.width(7)) comparator_1 (.a(opcode), .b(7'b1101111), .eq(comparator_1_eq));  // open: gt, lt
  Comparator #(.width(7)) comparator_2 (.a(opcode), .b(7'b1100111), .eq(comparator_2_eq));  // open: gt, lt
  or or_1 (or_1_out[0], comparator_1_eq, comparator_2_eq);
  Comparator #(.width(7)) comparator_3 (.a(opcode), .b(7'b0000011), .eq(or_1_out[1]));  // open: gt, lt
  Multiplexer #(.select(2), .width(2)) multiplexer_1 (
    .in0(2'b01), .in1(2'b10), .in2(2'b00), .out(WBSel), .sel(or_1_out));  // open: in3

  // Other names for the same wires on the sheet: full_code[9:0] = {funct3, opcode}
endmodule

module ASel_to_PCSel (
  input  [31:0] Instruction,
  input  ASel,
  output PCSel
);

  wire comparator_1_eq, comparator_2_eq, multiplexer_1_out, not_1_out, not_2_out;

  Comparator #(.width(7)) comparator_1 (.a(Instruction[6:0]), .b(7'b1100111), .eq(comparator_1_eq));  // open: gt, lt
  Multiplexer multiplexer_1 (.in0(ASel), .in1(not_1_out), .out(multiplexer_1_out), .sel(comparator_1_eq));
  not not_1 (not_1_out, ASel);
  Comparator #(.width(7)) comparator_2 (.a(Instruction[6:0]), .b(7'b0010111), .eq(comparator_2_eq));  // open: gt, lt
  and and_1 (PCSel, multiplexer_1_out, not_2_out);
  not not_2 (not_2_out, comparator_2_eq);

  // Other names for the same wires on the sheet: Opcode[6:0] = Instruction[6:0]
endmodule
