// Logisim project cpu.circ as structural Verilog: 3 circuits, main circuit cpu
module cpu (
  input  clk,
  input  [31:0] Instruction,
  input  [31:0] MemReadData,
  output [31:0] MemAddress,
  output [31:0] ProgramCounter,
  output [31:0] ra,
  output [31:0] sp,
  output [31:0] t0,
  output [31:0] t1,
  output [31:0] t2,
  output [31:0] s0,
  output [31:0] s1,
  output [31:0] a0,
  output [3:0] MemWriteMask,
  output [31:0] MemWriteData
);

  wire ASel, BrEq, BrLt, BrUn, BSel, Flush, MemWEn, PCSel, RegWEn;
  wire [1:0] WBSel;
  wire [2:0] funct3, ImmSel;
  wire [3:0] ALUSel;
  wire [4:0] rd, rs1, rs2;
  wire [6:0] funct7, opcode;
  wire [31:0] adder_1_out, DataToReg, imm, Instruction_t, multiplexer_1_out, multiplexer_2_out,
       multiplexer_3_out, multiplexer_4_out, multiplexer_5_out, ReadData1, ReadData2, Stage_2_PC_plus_4,
       Stage_2_ProgramCounter;

  Multiplexer #(.select(2), .width(32)) multiplexer_1 (
    .in0(DataToReg), .in1(MemAddress), .in2(Stage_2_PC_plus_4), .out(multiplexer_1_out), .sel(WBSel));  // open: in3
  Adder #(.width(32)) adder_1 (.a(ProgramCounter), .b(32'h4), .out(adder_1_out));  // open: cin, cout
  Multiplexer #(.width(32)) multiplexer_2 (
    .in0(ReadData1), .in1(Stage_2_ProgramCounter), .out(multiplexer_2_out), .sel(ASel));
  Multiplexer #(.width(32)) multiplexer_3 (.in0(ReadData2), .in1(imm), .out(multiplexer_3_out), .sel(BSel));
  Register #(.width(32)) u_Stage_2_PC_plus_4 (.D(adder_1_out), .clk(clk), .Q(Stage_2_PC_plus_4));  // open: en, clr
  Multiplexer #(.width(32)) multiplexer_4 (.in0(adder_1_out), .in1(MemAddress), .out(multiplexer_4_out), .sel(PCSel));
  alu alu_1 (.A(multiplexer_2_out), .B(multiplexer_3_out), .ALUSel(ALUSel), .ALUResult(MemAddress));
  cpu_ID cpu_id_1 (
    .Instruction(Instruction_t), .opcode(opcode), .rd(rd), .funct3(funct3), .rs1(rs1), .rs2(rs2),
    .funct7(funct7), .RegWEn(RegWEn));  // open: BSel, ASel_implied, ImmSel, MemWEn
  imm_gen imm_gen_1 (.Instruction(Instruction_t), .ImmSel(ImmSel), .Immediate(imm));
  regfile regfile_1 (
    .ReadIndex1(rs1), .ReadIndex2(rs2), .WriteIndex(rd), .WriteData(multiplexer_1_out), .RegWEn(RegWEn),
    .clk(clk), .ra(ra), .sp(sp), .t0(t0), .t1(t1), .t2(t2), .s0(s0), .s1(s1), .a0(a0), .ReadData1(ReadData1),
    .ReadData2(ReadData2));
  branch_comp branch_comp_1 (.BrData1(ReadData1), .BrData2(ReadData2), .BrUn(BrUn), .BrEq(BrEq), .BrLt(BrLt));
  partial_store partial_store_1 (
    .Instruction(Instruction_t), .MemAddress(MemAddress), .DataFromReg(ReadData2), .MemWEn(MemWEn),
    .MemWriteMask(MemWriteMask), .DataToMem(MemWriteData));
  partial_load partial_load_1 (
    .Instruction(Instruction_t), .MemAddress(MemAddress), .DataFromMem(MemReadData), .DataToReg(DataToReg));
  Register #(.width(32)) Stage_1_PC (.D(multiplexer_4_out), .clk(clk), .Q(ProgramCounter));  // open: en, clr
  Register #(.width(32)) Stage_2_PC (.D(ProgramCounter), .clk(clk), .Q(Stage_2_ProgramCounter));  // open: en, clr
  control_logic control_logic_1 (
    .Instruction(Instruction_t), .BrEq(BrEq), .BrLt(BrLt), .PCSel(PCSel), .ImmSel(ImmSel), .BrUn(BrUn),
    .ASel(ASel), .BSel(BSel), .ALUSel(ALUSel), .MemWEn(MemWEn), .WBSel(WBSel));  // open: RegWEn
  Multiplexer #(.width(32)) multiplexer_5 (.in0(Instruction), .in1(32'h13), .out(multiplexer_5_out), .sel(Flush));
  Register #(.width(32)) Stage_2_Instruction (.D(multiplexer_5_out), .clk(clk), .Q(Instruction_t));  // open: en, clr
  check_flush check_flush_1 (.ASel(ASel), .Instruction(Instruction_t), .Flush(Flush));

  // Other names for the same wires on the sheet: ALU_Result[31:0] = MemAddress; Preinstruction[31:0] = Instruction;
  //   Stage_1_ProgramCounter[31:0] = ProgramCounter

  // Notes on the sheet:
  //   To IMEM
  //   IMEM (do **NOT** move this)
  //   From IMEM
  //   Inputs/Outputs for testing. Do **NOT** move these.
  //   To DMEM
  //   DMEM (do **NOT** move this)
  //   From DMEM
endmodule

module cpu_ID (
  input  [31:0] Instruction,
  output [6:0] opcode,
  output [4:0] rd,
  output [2:0] funct3,
  output [4:0] rs1,
  output [4:0] rs2,
  output [6:0] funct7,
  output RegWEn,
  output BSel,
  output ASel_implied,
  output [2:0] ImmSel,
  output MemWEn
);

  wire ASel_B, ASel_J, BSel_I, BSel_I_star, BSel_U, comparator_1_eq, comparator_2_eq, comparator_3_eq,
       comparator_4_eq, comparator_5_eq, RegWEn_R;
  wire [2:0] funct3_B, funct3_I, funct3_I_star, funct3_R, funct3_S, ImmSel_B, ImmSel_I, ImmSel_J, ImmSel_S,
       ImmSel_U;
  wire [4:0] imm5_B, imm5_I_star, imm5_S, rd_I, rd_I_star, rd_J, rd_R, rd_U, rs1_B, rs1_I, rs1_I_star, rs1_R,
       rs1_S, rs2_B, rs2_R, rs2_S;
  wire [6:0] funct7_I_star, funct7_R, imm7_B, imm7_S, opcode_B, opcode_I, opcode_I_star, opcode_J, opcode_R,
       opcode_S, opcode_U;
  wire [11:0] imm12_I;
  wire [19:0] imm20_J, imm20_U;

  Comparator #(.width(7)) comparator_1 (.a(Instruction[6:0]), .b(7'b0010011), .eq(comparator_1_eq));  // open: gt, lt
  Comparator #(.width(7)) comparator_2 (.a(Instruction[6:0]), .b(7'b0000011), .eq(comparator_2_eq));  // open: gt, lt
  Comparator #(.width(7)) comparator_3 (.a(Instruction[6:0]), .b(7'b1100111), .eq(comparator_3_eq));  // open: gt, lt
  Comparator #(.width(7)) comparator_4 (.a(Instruction[6:0]), .b(7'b0010111), .eq(comparator_4_eq));  // open: gt, lt
  Comparator #(.width(7)) comparator_5 (.a(Instruction[6:0]), .b(7'b0110111), .eq(comparator_5_eq));  // open: gt, lt
  or or_1 (BSel_I, comparator_1_eq, comparator_2_eq, comparator_3_eq);
  Demultiplexer #(.width(3)) demultiplexer_1 (.out1(ImmSel_I), .in(3'b000), .sel(BSel_I));  // open: out0
  Comparator #(.width(7)) comparator_6 (.a(Instruction[6:0]), .b(7'b0110011), .eq(RegWEn_R));  // open: gt, lt
  Comparator #(.width(7)) comparator_7 (.a(Instruction[6:0]), .b(7'b0010011), .eq(BSel_I_star));  // open: gt, lt
  Comparator #(.width(7)) comparator_8 (.a(Instruction[6:0]), .b(7'b0100011), .eq(MemWEn));  // open: gt, lt
  Demultiplexer #(.width(3)) demultiplexer_2 (.out1(ImmSel_S), .in(3'b001), .sel(MemWEn));  // open: out0
  Comparator #(.width(7)) comparator_9 (.a(Instruction[6:0]), .b(7'b1100011), .eq(ASel_B));  // open: gt, lt
  Demultiplexer #(.width(3)) demultiplexer_3 (.out1(ImmSel_B), .in(3'b010), .sel(ASel_B));  // open: out0
  or or_2 (BSel_U, comparator_4_eq, comparator_5_eq);
  Demultiplexer #(.width(3)) demultiplexer_4 (.out1(ImmSel_U), .in(3'b011), .sel(BSel_U));  // open: out0
  Comparator #(.width(7)) comparator_10 (.a(Instruction[6:0]), .b(7'b1101111), .eq(ASel_J));  // open: gt, lt
  Demultiplexer #(.width(3)) demultiplexer_5 (.out1(ImmSel_J), .in(3'b100), .sel(ASel_J));  // open: out0
  Demultiplexer #(.enable("true"), .width(32)) demultiplexer_6 (
    .out1({imm12_I, rs1_I, funct3_I, rd_I, opcode_I}), .in(Instruction), .sel(BSel_I), .en(BSel_I));  // open: out0
  Demultiplexer #(.enable("true"), .width(32)) demultiplexer_7 (
    .out1({funct7_R, rs2_R, rs1_R, funct3_R, rd_R, opcode_R}), .in(Instruction), .sel(RegWEn_R), .en(RegWEn_R));  // open: out0
  Demultiplexer #(.enable("true"), .width(32)) demultiplexer_8 (
    .out1({funct7_I_star, imm5_I_star, rs1_I_star, funct3_I_star, rd_I_star, opcode_I_star}),
    .in(Instruction), .sel(BSel_I_star), .en(BSel_I_star));  // open: out0
  Demultiplexer #(.enable("true"), .width(32)) demultiplexer_9 (
    .out1({imm7_S, rs2_S, rs1_S, funct3_S, imm5_S, opcode_S}), .in(Instruction), .sel(MemWEn), .en(MemWEn));  // open: out0
  Demultiplexer #(.enable("true"), .width(32)) demultiplexer_10 (
    .out1({imm7_B, rs2_B, rs1_B, funct3_B, imm5_B, opcode_B}), .in(Instruction), .sel(ASel_B), .en(ASel_B));  // open: out0
  Demultiplexer #(.enable("true"), .width(32)) demultiplexer_11 (
    .out1({imm20_U, rd_U, opcode_U}), .in(Instruction), .sel(BSel_U), .en(BSel_U));  // open: out0
  Demultiplexer #(.enable("true"), .width(32)) demultiplexer_12 (
    .out1({imm20_J, rd_J, opcode_J}), .in(Instruction), .sel(ASel_J), .en(ASel_J));  // open: out0
  assign opcode = opcode_I | opcode_R | opcode_I_star | opcode_S | opcode_B | opcode_U | opcode_J;  // OR_Gate or_3, 7 bits wide
  assign rd = rd_I | rd_R | rd_I_star | rd_U | rd_J;  // OR_Gate or_4, 5 bits wide
  assign funct3 = funct3_R | funct3_I | funct3_I_star | funct3_S | funct3_B;  // OR_Gate or_5, 3 bits wide
  assign rs1 = rs1_R | rs1_I | rs1_I_star | rs1_S | rs1_B;  // OR_Gate or_6, 5 bits wide
  assign rs2 = rs2_R | rs2_S | rs2_B;  // OR_Gate or_7, 5 bits wide
  assign funct7 = funct7_R | funct7_I_star;  // OR_Gate or_8, 7 bits wide
  or or_9 (RegWEn, RegWEn_R, BSel_I, BSel_I_star, BSel_U, ASel_J);
  or or_10 (BSel, BSel_I, BSel_I_star, BSel_U, ASel_J, ASel_B);
  or or_11 (ASel_implied, ASel_B, ASel_J);
  assign ImmSel = ImmSel_J | ImmSel_I | ImmSel_S | ImmSel_B | ImmSel_U;  // OR_Gate or_12, 3 bits wide

  // Other names for the same wires on the sheet: BSel_B = ASel_B; Opcode_t[6:0] = Instruction[6:0]; RegWEn_I = BSel_I;
  //   RegWEn_I_star = BSel_I_star; BSel_J = ASel_J; RegWEn_J = ASel_J; RegWEn_U = BSel_U
endmodule

module check_flush (
  input  ASel,
  input  [31:0] Instruction,
  output Flush
);

  wire and_1_out, comparator_1_eq, comparator_2_eq, comparator_3_eq, comparator_4_eq, or_1_out;

  Comparator #(.width(7)) comparator_1 (.a(Instruction[6:0]), .b(7'b1100011), .eq(comparator_1_eq));  // open: gt, lt
  Comparator #(.width(1)) comparator_2 (.a(ASel), .b(1'b1), .eq(comparator_2_eq));  // open: gt, lt
  Comparator #(.width(7)) comparator_3 (.a(Instruction[6:0]), .b(7'b1101111), .eq(comparator_3_eq));  // open: gt, lt
  Comparator #(.width(7)) comparator_4 (.a(Instruction[6:0]), .b(7'b1100111), .eq(comparator_4_eq));  // open: gt, lt
  and and_1 (and_1_out, comparator_1_eq, comparator_2_eq);
  or or_1 (or_1_out, comparator_3_eq, comparator_4_eq);
  or or_2 (Flush, and_1_out, or_1_out);

  // Other names for the same wires on the sheet: Opcode[6:0] = Instruction[6:0]
endmodule
