// Logisim project imm-gen.circ as structural Verilog: 7 circuits, main circuit imm_gen
module imm_gen (
  input  [31:0] Instruction,
  input  [2:0] ImmSel,
  output [31:0] Immediate
);

  wire [31:0] generate_b_1_immediate, generate_i_1_immediate, generate_j_1_immediate, generate_s_1_immediate,
       generate_u_1_immediate;

  generate_i generate_i_1 (.Instruction(Instruction), .Immediate(generate_i_1_immediate));
  generate_s generate_s_1 (.INSTRUCTION(Instruction), .IMMEDIATE(generate_s_1_immediate));
  generate_b generate_b_1 (.INSTRUCTION(Instruction), .IMMEDIATE(generate_b_1_immediate));
  generate_u generate_u_1 (.INSTRUCTION(Instruction), .IMMEDIATE(generate_u_1_immediate));
  Multiplexer #(.select(3), .width(32)) multiplexer_1 (
    .in0(generate_i_1_immediate), .in1(generate_s_1_immediate), .in2(generate_b_1_immediate),
    .in3(generate_u_1_immediate), .in4(generate_j_1_immediate), .out(Immediate), .sel(ImmSel));  // open: in5, in6, in7
  generate_j generate_j_1 (.INSTRUCTION(Instruction), .IMMEDIATE(generate_j_1_immediate));

  // Notes on the sheet:
  //   INPUTS to your circuit
  //   DON'T CHANGE THE LOCATIONS OF THE INPUTS AND OUTPUTS!
  //   OUTPUT from your circuit
endmodule

module generate_i (
  input  [31:0] Instruction,
  output [31:0] Immediate
);

  assign Immediate = {{20{Instruction[31]}}, Instruction[31:20]};  // Bit_Extender bit_extender_1
endmodule

module generate_i_star (
  input  [31:0] INSTRUCTION,
  output [31:0] IMMEDIATE
);

  assign IMMEDIATE = {{27{INSTRUCTION[24]}}, INSTRUCTION[24:20]};  // Bit_Extender bit_extender_1
endmodule

module generate_s (
  input  [31:0] INSTRUCTION,
  output [31:0] IMMEDIATE
);

  assign IMMEDIATE = {{20{INSTRUCTION[31]}}, {INSTRUCTION[31:25], INSTRUCTION[11:7]}};  // Bit_Extender bit_extender_1
endmodule

module generate_b (
  input  [31:0] INSTRUCTION,
  output [31:0] IMMEDIATE
);

  assign IMMEDIATE = {{19{INSTRUCTION[31]}}, {INSTRUCTION[31], INSTRUCTION[7], INSTRUCTION[30:25], INSTRUCTION[11:8], 1'b0}};  // Bit_Extender bit_extender_1
endmodule

module generate_u (
  input  [31:0] INSTRUCTION,
  output [31:0] IMMEDIATE
);


  assign IMMEDIATE = {INSTRUCTION[31:12], {12{1'b0}}};
endmodule

module generate_j (
  input  [31:0] INSTRUCTION,
  output [31:0] IMMEDIATE
);

  assign IMMEDIATE = {{11{INSTRUCTION[31]}}, {INSTRUCTION[31], INSTRUCTION[19:12], INSTRUCTION[20], INSTRUCTION[30:21], 1'b0}};  // Bit_Extender bit_extender_1
endmodule
