// Logisim project partial-store.circ as structural Verilog: 2 circuits, main circuit partial_store
module partial_store (
  input  [31:0] Instruction,
  input  [31:0] MemAddress,
  input  [31:0] DataFromReg,
  input  MemWEn,
  output [3:0] MemWriteMask,
  output [31:0] DataToMem
);

  wire RegWEn;
  wire [2:0] funct3;
  wire [3:0] multiplexer_1_out, multiplexer_2_out, multiplexer_5_out;
  wire [4:0] rd, rs1, rs2;
  wire [6:0] funct7, opcode;
  wire [31:0] multiplexer_3_out, multiplexer_4_out;

  Multiplexer #(.select(2), .width(4)) multiplexer_1 (
    .in0(4'b0001), .in1(4'b0010), .in2(4'b0100), .in3(4'b1000), .out(multiplexer_1_out), .sel(MemAddress[1:0]));
  Multiplexer #(.select(2), .width(4)) multiplexer_2 (
    .in0(4'b0011), .in2(4'b1100), .out(multiplexer_2_out), .sel(MemAddress[1:0]));  // open: in1, in3
  partial_store_ID partial_store_id_1 (
    .Instruction(Instruction), .opcode(opcode), .rd(rd), .funct3(funct3), .rs1(rs1), .rs2(rs2),
    .funct7(funct7), .RegWEn(RegWEn));  // open: BSel, ASel_implied, ImmSel
  Multiplexer #(.select(2), .width(32)) multiplexer_3 (
    .in0({{24{1'b0}}, DataFromReg[7:0]}), .in1({{16{1'b0}}, DataFromReg[7:0], {8{1'b0}}}),
    .in2({{8{1'b0}}, DataFromReg[7:0], {16{1'b0}}}), .in3({DataFromReg[7:0], {24{1'b0}}}),
    .out(multiplexer_3_out), .sel(MemAddress[1:0]));
  Multiplexer #(.select(2), .width(32)) multiplexer_4 (
    .in0({{16{1'b0}}, DataFromReg[15:0]}), .in2({DataFromReg[15:0], {16{1'b0}}}), .out(multiplexer_4_out),
    .sel(MemAddress[1:0]));  // open: in1, in3
  Multiplexer #(.select(3), .width(4)) multiplexer_5 (
    .in0(multiplexer_1_out), .in1(multiplexer_2_out), .in2(4'b1111), .out(multiplexer_5_out), .sel(funct3));  // open: in3, in4, in5, in6, in7
  Multiplexer #(.width(4)) multiplexer_6 (.in0(4'b0000), .in1(multiplexer_5_out), .out(MemWriteMask), .sel(MemWEn));
  Multiplexer #(.select(3), .width(32)) multiplexer_7 (
    .in0(multiplexer_3_out), .in1(multiplexer_4_out), .in2(DataFromReg), .out(DataToMem), .sel(funct3));  // open: in3, in4, in5, in6, in7

  // Other names for the same wires on the sheet: Bottom2[1:0] = MemAddress[1:0]

  // Notes on the sheet:
  //   INPUTS to your circuit
  //   DON'T CHANGE THE LOCATIONS OF THE INPUTS AND OUTPUTS!
  //   OUTPUT from your circuit
endmodule

module partial_store_ID (
  input  [31:0] Instruction,
  output [6:0] opcode,
  output [4:0] rd,
  output [2:0] funct3,
  output [4:0] rs1,
  output [4:0] rs2,
  output [6:0] funct7,
  output RegWEn,
  output BSel,
  output ASel_implied,
  output [2:0] ImmSel
);

  wire ASel_B, ASel_J, BSel_I, BSel_I_star, BSel_U, comparator_1_eq, comparator_2_eq, comparator_5_eq,
       RegWEn_R;
  wire [2:0] funct3_B, funct3_I, funct3_I_star, funct3_R, funct3_S, ImmSel_B, ImmSel_I, ImmSel_J, ImmSel_S,
       ImmSel_U;
  wire [4:0] imm5_B, imm5_I_star, imm5_S, rd_I, rd_I_star, rd_J, rd_R, rd_U, rs1_B, rs1_I, rs1_I_star, rs1_R,
       rs1_S, rs2_B, rs2_R, rs2_S;
  wire [6:0] funct7_I_star, funct7_R, imm7_B, imm7_S, opcode_B, opcode_I, opcode_I_star, opcode_J, opcode_R,
       opcode_S, opcode_U;
  wire [11:0] imm12_I;
  wire [19:0] imm20_J, imm20_U;

  Comparator #(.width(7)) comparator_1 (.a(Instruction[6:0]), .b(7'b0010011), .eq(comparator_1_eq));  // open: gt, lt
  Comparator #(.width(7)) comparator_2 (.a(Instruction[6:0]), .b(7'b0000011), .eq(comparator_2_eq));  // open: gt, lt
  or or_1 (BSel_I, comparator_1_eq, comparator_2_eq);
  Demultiplexer #(.width(3)) demultiplexer_1 (.out1(ImmSel_I), .in(3'b000), .sel(BSel_I));  // open: out0
  Comparator #(.width(7)) comparator_3 (.a(Instruction[6:0]), .b(7'b0110011), .eq(RegWEn_R));  // open: gt, lt
  Comparator #(.width(7)) comparator_4 (.a(Instruction[6:0]), .b(7'b0010011), .eq(BSel_I_star));  // open: gt, lt
  Comparator #(.width(7)) comparator_5 (.a(Instruction[6:0]), .b(7'b0100011), .eq(comparator_5_eq));  // open: gt, lt
  Demultiplexer #(.width(3)) demultiplexer_2 (.out1(ImmSel_S), .in(3'b001), .sel(comparator_5_eq));  // open: out0
  Comparator #(.width(7)) comparator_6 (.a(Instruction[6:0]), .b(7'b1100011), .eq(ASel_B));  // open: gt, lt
  Demultiplexer #(.width(3)) demultiplexer_3 (.out1(ImmSel_B), .in(3'b010), .sel(ASel_B));  // open: out0
  Comparator #(.width(7)) comparator_7 (.a(Instruction[6:0]), .b(7'b0010111), .eq(BSel_U));  // open: gt, lt
  Demultiplexer #(.width(3)) demultiplexer_4 (.out1(ImmSel_U), .in(3'b011), .sel(BSel_U));  // open: out0
  Comparator #(.width(7)) comparator_8 (.a(Instruction[6:0]), .b(7'b1101111), .eq(ASel_J));  // open: gt, lt
  Demultiplexer #(.width(3)) demultiplexer_5 (.out1(ImmSel_J), .in(3'b100), .sel(ASel_J));  // open: out0
  Demultiplexer #(.enable("true"), .width(32)) demultiplexer_6 (
    .out1({imm12_I, rs1_I, funct3_I, rd_I, opcode_I}), .in(Instruction), .sel(BSel_I), .en(BSel_I));  // open: out0
  Demultiplexer #(.enable("true"), .width(32)) demultiplexer_7 (
    .out1({funct7_R, rs2_R, rs1_R, funct3_R, rd_R, opcode_R}), .in(Instruction), .sel(RegWEn_R), .en(RegWEn_R));  // open: out0
  Demultiplexer #(.enable("true"), .width(32)) demultiplexer_8 (
    .out1({funct7_I_star, imm5_I_star, rs1_I_star, funct3_I_star, rd_I_star, opcode_I_star}),
    .in(Instruction), .sel(BSel_I_star), .en(BSel_I_star));  // open: out0
  Demultiplexer #(.enable("true"), .width(32)) demultiplexer_9 (
    .out1({imm7_S, rs2_S, rs1_S, funct3_S, imm5_S, opcode_S}), .in(Instruction), .sel(comparator_5_eq),
    .en(comparator_5_eq));  // open: out0
  Demultiplexer #(.enable("true"), .width(32)) demultiplexer_10 (
    .out1({imm7_B, rs2_B, rs1_B, funct3_B, imm5_B, opcode_B}), .in(Instruction), .sel(ASel_B), .en(ASel_B));  // open: out0
  Demultiplexer #(.enable("true"), .width(32)) demultiplexer_11 (
    .out1({imm20_U, rd_U, opcode_U}), .in(Instruction), .sel(BSel_U), .en(BSel_U));  // open: out0
  Demultiplexer #(.enable("true"), .width(32)) demultiplexer_12 (
    .out1({imm20_J, rd_J, opcode_J}), .in(Instruction), .sel(ASel_J), .en(ASel_J));  // open: out0
  assign opcode = opcode_I | opcode_R | opcode_I_star | opcode_S | opcode_B | opcode_U | opcode_J;  // OR_Gate or_2, 7 bits wide
  assign rd = rd_I | rd_R | rd_I_star | rd_U | rd_J;  // OR_Gate or_3, 5 bits wide
  assign funct3 = funct3_R | funct3_I | funct3_I_star | funct3_S | funct3_B;  // OR_Gate or_4, 3 bits wide
  assign rs1 = rs1_R | rs1_I | rs1_I_star | rs1_S | rs1_B;  // OR_Gate or_5, 5 bits wide
  assign rs2 = rs2_R | rs2_S | rs2_B;  // OR_Gate or_6, 5 bits wide
  assign funct7 = funct7_R | funct7_I_star;  // OR_Gate or_7, 7 bits wide
  or or_8 (RegWEn, RegWEn_R, BSel_I, BSel_I_star, BSel_U, ASel_J);
  or or_9 (BSel, BSel_I, BSel_I_star, BSel_U, ASel_J, ASel_B);
  or or_10 (ASel_implied, ASel_B, ASel_J);
  assign ImmSel = ImmSel_J | ImmSel_I | ImmSel_S | ImmSel_B | ImmSel_U;  // OR_Gate or_11, 3 bits wide

  // Other names for the same wires on the sheet: BSel_B = ASel_B; Opcode_t[6:0] = Instruction[6:0]; RegWEn_I = BSel_I;
  //   RegWEn_I_star = BSel_I_star; BSel_J = ASel_J; RegWEn_J = ASel_J; RegWEn_U = BSel_U
endmodule
