// Logisim project regfile.circ as structural Verilog: 1 circuit, main circuit regfile
module regfile (
  input  [4:0] ReadIndex1,
  input  [4:0] ReadIndex2,
  input  [4:0] WriteIndex,
  input  [31:0] WriteData,
  input  RegWEn,
  input  clk,
  output [31:0] ra,
  output [31:0] sp,
  output [31:0] t0,
  output [31:0] t1,
  output [31:0] t2,
  output [31:0] s0,
  output [31:0] s1,
  output [31:0] a0,
  output [31:0] ReadData1,
  output [31:0] ReadData2
);

  wire WE0, WE1, WE2, WE3, WE4, WE5, WE6, WE7, WE8, WE9, WE10, WE11, WE12, WE13, WE14, WE15, WE16, WE17,
       WE18, WE19, WE20, WE21, WE22, WE23, WE24, WE25, WE26, WE27, WE28, WE29, WE30, WE31;
  wire [31:0] a1, a2, a3, a4, a5, a6, a7, gp, s2, s3, s4, s5, s6, s7, s8, s9, s10, s11, t3, t4, t5, t6, tp,
       zero;

  Demultiplexer #(.enable("true"), .select(5)) demultiplexer_1 (
    .out0(WE0), .out1(WE1), .out2(WE2), .out3(WE3), .out4(WE4), .out5(WE5), .out6(WE6), .out7(WE7),
    .out8(WE8), .out9(WE9), .out10(WE10), .out11(WE11), .out12(WE12), .out13(WE13), .out14(WE14),
    .out15(WE15), .out16(WE16), .out17(WE17), .out18(WE18), .out19(WE19), .out20(WE20), .out21(WE21),
    .out22(WE22), .out23(WE23), .out24(WE24), .out25(WE25), .out26(WE26), .out27(WE27), .out28(WE28),
    .out29(WE29), .out30(WE30), .out31(WE31), .in(1'b1), .sel(WriteIndex), .en(RegWEn));
  Multiplexer #(.select(5), .width(32)) multiplexer_1 (
    .in0(zero), .in1(ra), .in2(sp), .in3(gp), .in4(tp), .in5(t0), .in6(t1), .in7(t2), .in8(s0), .in9(s1),
    .in10(a0), .in11(a1), .in12(a2), .in13(a3), .in14(a4), .in15(a5), .in16(a6), .in17(a7), .in18(s2),
    .in19(s3), .in20(s4), .in21(s5), .in22(s6), .in23(s7), .in24(s8), .in25(s9), .in26(s10), .in27(s11),
    .in28(t3), .in29(t4), .in30(t5), .in31(t6), .out(ReadData1), .sel(ReadIndex1));
  Multiplexer #(.select(5), .width(32)) multiplexer_2 (
    .in0(zero), .in1(ra), .in2(sp), .in3(gp), .in4(tp), .in5(t0), .in6(t1), .in7(t2), .in8(s0), .in9(s1),
    .in10(a0), .in11(a1), .in12(a2), .in13(a3), .in14(a4), .in15(a5), .in16(a6), .in17(a7), .in18(s2),
    .in19(s3), .in20(s4), .in21(s5), .in22(s6), .in23(s7), .in24(s8), .in25(s9), .in26(s10), .in27(s11),
    .in28(t3), .in29(t4), .in30(t5), .in31(t6), .out(ReadData2), .sel(ReadIndex2));
  Register #(.width(32)) register_1 (.D(WriteData), .en(WE31), .clk(clk), .Q(t6));  // open: clr
  Register #(.width(32)) register_2 (.D(WriteData), .en(WE22), .clk(clk), .Q(s6));  // open: clr
  Register #(.width(32)) register_3 (.D(WriteData), .en(WE13), .clk(clk), .Q(a3));  // open: clr
  Register #(.width(32)) register_4 (.D(WriteData), .en(WE3), .clk(clk), .Q(gp));  // open: clr
  Register #(.width(32)) register_5 (.D(WriteData), .en(WE30), .clk(clk), .Q(t5));  // open: clr
  Register #(.width(32)) register_6 (.D(WriteData), .en(WE21), .clk(clk), .Q(s5));  // open: clr
  Register #(.width(32)) register_7 (.D(WriteData), .en(WE12), .clk(clk), .Q(a2));  // open: clr
  Register #(.width(32)) register_8 (.D(WriteData), .en(WE2), .clk(clk), .Q(sp));  // open: clr
  Register #(.width(32)) register_9 (.D(WriteData), .en(WE29), .clk(clk), .Q(t4));  // open: clr
  Register #(.width(32)) register_10 (.D(WriteData), .en(WE20), .clk(clk), .Q(s4));  // open: clr
  Register #(.width(32)) register_11 (.D(WriteData), .en(WE11), .clk(clk), .Q(a1));  // open: clr
  Register #(.width(32)) register_12 (.D(WriteData), .en(WE1), .clk(clk), .Q(ra));  // open: clr
  Register #(.width(32)) register_13 (.D(WriteData), .en(WE28), .clk(clk), .Q(t3));  // open: clr
  Register #(.width(32)) register_14 (.D(WriteData), .en(WE19), .clk(clk), .Q(s3));  // open: clr
  Register #(.width(32)) register_15 (.D(WriteData), .en(WE10), .clk(clk), .Q(a0));  // open: clr
  Register #(.width(32)) register_16 (.D({32{1'b0}}), .en(WE0), .clk(clk), .Q(zero));  // open: clr
  Register #(.width(32)) register_17 (.D(WriteData), .en(WE27), .clk(clk), .Q(s11));  // open: clr
  Register #(.width(32)) register_18 (.D(WriteData), .en(WE18), .clk(clk), .Q(s2));  // open: clr
  Register #(.width(32)) register_19 (.D(WriteData), .en(WE9), .clk(clk), .Q(s1));  // open: clr
  Register #(.width(32)) register_20 (.D(WriteData), .en(WE8), .clk(clk), .Q(s0));  // open: clr
  Register #(.width(32)) register_21 (.D(WriteData), .en(WE26), .clk(clk), .Q(s10));  // open: clr
  Register #(.width(32)) register_22 (.D(WriteData), .en(WE17), .clk(clk), .Q(a7));  // open: clr
  Register #(.width(32)) register_23 (.D(WriteData), .en(WE25), .clk(clk), .Q(s9));  // open: clr
  Register #(.width(32)) register_24 (.D(WriteData), .en(WE16), .clk(clk), .Q(a6));  // open: clr
  Register #(.width(32)) register_25 (.D(WriteData), .en(WE7), .clk(clk), .Q(t2));  // open: clr
  Register #(.width(32)) register_26 (.D(WriteData), .en(WE24), .clk(clk), .Q(s8));  // open: clr
  Register #(.width(32)) register_27 (.D(WriteData), .en(WE6), .clk(clk), .Q(t1));  // open: clr
  Register #(.width(32)) register_28 (.D(WriteData), .en(WE15), .clk(clk), .Q(a5));  // open: clr
  Register #(.width(32)) register_29 (.D(WriteData), .en(WE5), .clk(clk), .Q(t0));  // open: clr
  Register #(.width(32)) register_30 (.D(WriteData), .en(WE23), .clk(clk), .Q(s7));  // open: clr
  Register #(.width(32)) register_31 (.D(WriteData), .en(WE14), .clk(clk), .Q(a4));  // open: clr
  Register #(.width(32)) register_32 (.D(WriteData), .en(WE4), .clk(clk), .Q(tp));  // open: clr

  // Notes on the sheet:
  //   INPUTS to your circuit
  //   DON'T CHANGE THE LOCATIONS OF THE INPUTS AND OUTPUTS!
  //   These are DEBUG/TEST outputs from your circuit.
  //   OUTPUTS from your circuit
endmodule
